# Fritzing sketch main-wiring (saved by Fritzing 1.0.1rc)
breadboards: 1

parts:
  Mod1 = Raspberry Pi 4B
  Part1 = Breadboard Power Supply Board SMD
  M1 = gy9250

nets:
  GND: Mod1.GND, Part1.GND
  N1: Part1.VCC, M1.pin2, M1.pin6
  N2: M1.pin4, M1.pin10
  N3: M1.pin7, M1.pin9

custom parts:
  gy9250: MPU-9250 module (three-axis gyroscope + three-axis acceleration + three-axis magnetic field). The generic model from ebay et. al. rather than the Sparkfun version.
